# Fritzing sketch MH_board_v4 (saved by Fritzing 0.8.3b)
breadboards: 1

parts:
  DIN1 = DIN-5 jack (MIDI) [package=THT]
  Bauteil1 = Arduino Mega 2560 (Rev3)
  R1 = Resistor [tolerance=±5% resistance=220 package=THT]
  S1 = Pushbutton [package="[THT]"]
  S2 = Pushbutton [package="[THT]"]
  S3 = Pushbutton [package="[THT]"]
  S4 = Pushbutton [package="[THT]"]
  S5 = Pushbutton [package="[THT]"]
  S6 = Pushbutton [package="[THT]"]
  S7 = Pushbutton [package="[THT]"]
  S8 = Pushbutton [package="[THT]"]
  R11 = Resistor [tolerance=±5% resistance=220 package=THT]

nets:
  N1: DIN1.5, R11.Pin_1
  N2: DIN1.2, Bauteil1.GND, S1.Pin_3, S1.Pin_4, S2.Pin_3, S2.Pin_4, S3.Pin_3, S3.Pin_4, S4.Pin_3, S4.Pin_4, S5.Pin_3, S5.Pin_4, S6.Pin_3, S6.Pin_4, S7.Pin_3, S7.Pin_4, S8.Pin_3, S8.Pin_4
  N3: DIN1.4, R1.Pin_0
  N4: Bauteil1.D9_PWM, S7.Pin_1, S7.Pin_2
  N5: Bauteil1.D8_PWM, S5.Pin_1, S5.Pin_2
  N6: Bauteil1.5V, R1.Pin_1
  N7: Bauteil1.D1_TX0, R11.Pin_0
  N8: Bauteil1.D2_PWM, S1.Pin_1, S1.Pin_2
  N9: Bauteil1.D3_PWM, S2.Pin_1, S2.Pin_2
  N10: Bauteil1.D4_PWM, S3.Pin_1, S3.Pin_2
  N11: Bauteil1.D5_PWM, S4.Pin_1, S4.Pin_2
  N12: Bauteil1.D6_PWM, S8.Pin_1, S8.Pin_2
  N13: Bauteil1.D7_PWM, S6.Pin_1, S6.Pin_2
